// Logisim project components.circ as structural Verilog: 1 circuit, main circuit main
module main (
  input  [3:0] A,
  input  in_2,
  input  [3:0] B,
  input  in_4,
  input  in_5,
  input  in_6,
  input  [2:0] ALU_Ctrl,
  input  [1:0] in_8,
  input  [1:0] in_9,
  input  in_10,
  input  in_11,
  input  in_12,
  input  in_13,
  input  in_14,
  input  in_15,
  input  in_16,
  input  in_17,
  input  in_18,
  input  in_19,
  input  in_20,
  input  in_21,
  input  in_22,
  input  in_23,
  input  in_24,
  output out_25,
  output [3:0] out_26,
  output out_27,
  output out_28,
  output out_29,
  output out_30,
  output [3:0] out_31,
  output [3:0] out_32,
  output out_33,
  output out_34,
  output [3:0] out_35,
  output out_36,
  output [3:0] out_37,
  output out_38,
  output out_39,
  output out_40,
  output out_41,
  output out_42,
  output out_43,
  output out_44,
  output out_45,
  output out_46,
  output out_47,
  output out_48,
  output out_49,
  output out_50,
  output out_51,
  output out_52,
  output out_53,
  output out_54
);

  wire and_2_out, and_3_out, clock_1_out, clock_2_out, clock_3_out, clock_4_out, clock_5_out, clock_6_out,
       d_ff_6_qn, d_ff_7_qn, d_ff_8_qn, d_ff_9_qn, xor_2_out;
  wire [3:0] multiplexer_2_out, not_1_out;

  Clock clock_1 (.out(clock_1_out));
  Clock clock_2 (.out(clock_2_out));
  xor xor_1 (out_33, in_10, in_12);
  and and_1 (out_36, in_10, in_12);
  D_Flip_Flop d_ff_1 (.D(in_15), .clk(clock_1_out), .Q(out_43));  // open: Qn, preset, reset
  S_R_Flip_Flop s_r_ff_1 (.S(in_19), .R(in_21), .clk(clock_2_out), .Q(out_47), .Qn(out_51));  // open: reset, preset
  Multiplexer #(.select(2), .enable("false")) multiplexer_1 (
    .in0(in_2), .in1(in_4), .in2(in_5), .in3(in_6), .out(out_27), .sel(in_8));
  D_Flip_Flop d_ff_2 (.D(in_16), .clk(clock_1_out), .Q(out_44));  // open: Qn, preset, reset
  Clock clock_3 (.out(clock_3_out));
  Decoder #(.select(2), .enable("false")) decoder_1 (
    .out0(out_25), .out1(out_28), .out2(out_29), .out3(out_30), .sel(in_9));
  xor xor_2 (xor_2_out, in_11, in_13);
  and and_2 (and_2_out, in_11, in_13);
  D_Flip_Flop d_ff_3 (.D(in_22), .clk(clock_3_out), .Q(out_48), .Qn(out_52));  // open: preset, reset
  D_Flip_Flop d_ff_4 (.D(in_17), .clk(clock_1_out), .Q(out_45));  // open: Qn, preset, reset
  and and_3 (and_3_out, in_14, xor_2_out);
  D_Flip_Flop d_ff_5 (.D(in_18), .clk(clock_1_out), .Q(out_46));  // open: Qn, preset, reset
  Clock clock_4 (.out(clock_4_out));
  xor xor_3 (out_34, xor_2_out, in_14);
  or or_1 (out_38, and_2_out, and_3_out);
  T_Flip_Flop t_ff_1 (.T(in_23), .clk(clock_4_out), .Q(out_49), .Qn(out_53));  // open: reset, preset
  Clock clock_5 (.out(clock_5_out));
  D_Flip_Flop d_ff_6 (.D(d_ff_6_qn), .clk(clock_5_out), .Q(out_39), .Qn(d_ff_6_qn));  // open: preset, reset
  Clock clock_6 (.out(clock_6_out));
  assign not_1_out = ~B;  // NOT_Gate not_1, 4 bits wide
  D_Flip_Flop d_ff_7 (.D(d_ff_7_qn), .clk(d_ff_6_qn), .Q(out_40), .Qn(d_ff_7_qn));  // open: preset, reset
  J_K_Flip_Flop j_k_ff_1 (.J(in_20), .K(in_24), .clk(clock_6_out), .Q(out_50), .Qn(out_54));  // open: preset, reset
  Multiplexer #(.width(4), .enable("false")) multiplexer_2 (
    .in0(B), .in1(not_1_out), .out(multiplexer_2_out), .sel(ALU_Ctrl[0]));
  assign out_32 = A & B;  // AND_Gate and_4, 4 bits wide
  assign out_35 = A | B;  // OR_Gate or_2, 4 bits wide
  assign out_37 = A ^ B;  // XOR_Gate xor_4, 4 bits wide
  D_Flip_Flop d_ff_8 (.D(d_ff_8_qn), .clk(d_ff_7_qn), .Q(out_41), .Qn(d_ff_8_qn));  // open: preset, reset
  Adder #(.width(4)) adder_1 (.a(A), .b(multiplexer_2_out), .out(out_26), .cin(ALU_Ctrl[0]));  // open: cout
  D_Flip_Flop d_ff_9 (.D(d_ff_9_qn), .clk(d_ff_8_qn), .Q(out_42), .Qn(d_ff_9_qn));  // open: preset, reset
  Multiplexer #(.select(3), .width(4), .enable("false")) multiplexer_3 (
    .in0(out_26), .in1(out_26), .in2(out_32), .in3(out_35), .in4(out_37), .out(out_31), .sel(ALU_Ctrl));  // open: in5, in6, in7
endmodule
